# Fritzing sketch help-digital (saved by Fritzing 0.9.3b)
perfboards: 1

parts:
  J1 = shrouded pin header, 10 pins [form="♂ (shrouded male)"]  # not connected
  J2 = shrouded pin header, 10 pins [form="♂ (shrouded male)"]
  R1 = Resistor [tolerance=±5% resistance=1k package=THT]
  Q2 = NPN-Transistor [package="TO92 [THT]"]
  J3 = female pin header, 2 pins [form="♀ (female)"]
  J4 = female pin header, 2 pins [form="♀ (female)"]  # not connected
  Q3 = NPN-Transistor [package="TO92 [THT]"]  # not connected
  D4 = Rectifier Diode [part_number=1N4001 package="300 mil [THT]"]
  R2 = Resistor [tolerance=±5% resistance=1k package=THT]
  Q4 = NPN-Transistor [package="TO92 [THT]"]
  D5 = Rectifier Diode [part_number=1N4001 package="300 mil [THT]"]
  J5 = female pin header, 2 pins [form="♀ (female)"]
  D6 = Rectifier Diode [part_number=1N4001 package="300 mil [THT]"]  # not connected

nets:
  N1: J2.pin1, R2.Pin_0
  N2: J2.pin8, R1.Pin_1
  N3: R1.Pin_0, Q2.B
  N4: Q2.E, J3.pin1, D4.anode
  N5: R2.Pin_1, Q4.B
  N6: Q4.E, D5.anode, J5.pin1

notes:
  1  2  3  4  5
  10 9  8  7  6
